# Fritzing sketch fifth year project (saved by Fritzing 0.9.5d)
breadboards: 2

parts:
  Part1 = Arduino Uno (Rev3) - ICSP
  Part2 = 16-Channel 12-bit PWM Servo Driver - I2C [part_number=815]
  e-radionica1 = TCS230 Color Sensor [part_number=101209]
  M1 = Dagu DGServo 9g (Pan and tilt) [part_number=RS001B]
  M2 = DC Motor
  M8 = fc-51 [package=THT]
  M9 = fc-51 [package=THT]
  S1 = H-Bridge with L298N
  M3 = Dagu DGServo 9g (Pan and tilt) [part_number=RS001B]
  M10 = Dagu DGServo 9g (Pan and tilt) [part_number=RS001B]
  M11 = Dagu DGServo 9g (Pan and tilt) [part_number=RS001B]
  M12 = Dagu DGServo 9g (Pan and tilt) [part_number=RS001B]
  LCD2004-I2C1 = LCD2004-I2C

nets:
  N1: Part1.A4/SDA, Part2.SDA, LCD2004-I2C1.SCL
  N2: Part1.A5/SCL, Part2.SCL, LCD2004-I2C1.SDA
  VCC: Part1.5V, Part2.VCC, e-radionica1.Vcc, M8.pin3, M9.pin3, S1.5V, LCD2004-I2C1.VCC
  N3: Part1.D8, e-radionica1.Out
  N4: Part1.D11_PWM/MOSI, M8.pin1
  N5: Part1.D12/MISO, M9.pin1
  N6: Part1.D2, S1.IN1
  N7: Part1.D3_PWM, S1.IN2
  N8: Part1.D4, e-radionica1.S0
  N9: Part1.D5_PWM, e-radionica1.S1
  N10: Part1.D6_PWM, e-radionica1.S2
  N11: Part1.D7, e-radionica1.S3
  GND: Part1.GND, Part2.GND, e-radionica1.Gnd, M1.gnd, M8.pin2, M9.pin2, S1.GND, M3.gnd, M10.gnd, M11.gnd, M12.gnd, LCD2004-I2C1.GND
  N12: Part2.PWM4, M10.pulse
  VCC_2: Part2.5.0V, M1.vcc, M3.vcc, M10.vcc, M11.vcc, M12.vcc
  N13: Part2.PWM1, M1.pulse
  N14: Part2.PWM0, M3.pulse
  N15: Part2.PWM12, M12.pulse
  N16: Part2.PWM8, M11.pulse
  N17: M2.pin_1, S1.M1-02, S1.M2-01, S1.M2-02, S1.ENA-5V, S1.ENB-5V
  N18: M2.pin_2, S1.M1-01

custom parts:
  16-Channel 12-bit PWM Servo Driver - I2C: You want to make a cool robot, maybe a hexapod walker, or maybe just a piece of art with a lot of moving parts. Or maybe you want to drive a lot of LEDs with precise PWM output. Using only two pins, control 16 free-running PWM outputs! You can even chain up 62 breakouts to control up to 992 PWM outputs.
  TCS230 Color Sensor: TCS230
  H-Bridge with L298N: h-bridge
  LCD2004-I2C: A standard character display with 4x20 characters. Comes in many colors with LCM2004 IIC attached.
